// Digital circuit detetorBorda.dig as structural Verilog
module detetorBorda (
  input  Ck,
  output Subida,
  output Descida
);

  wire not_1_out, not_2_out, not_3_out, not_4_out, not_5_out, not_6_out;

  not not_1 (not_1_out, Ck);
  not not_2 (not_2_out, Ck);
  not not_3 (not_3_out, not_1_out);
  not not_4 (not_4_out, not_2_out);
  not not_5 (not_5_out, not_3_out);
  not not_6 (not_6_out, not_4_out);
  and and_1 (Subida, Ck, not_5_out);
  nor nor_1 (Descida, Ck, not_6_out);
endmodule
